# Fritzing sketch DemoSetUp (saved by Fritzing 0.9.4)
circuit board: 18.7522cm x 11.5506cm
breadboards: 2

parts:
  VictimOLED = OLED 128x64 I2C Monochrome Display
  AttackerOLED = OLED 128x64 I2C Monochrome Display
  RequesterOLED = OLED 128x64 I2C Monochrome Display
  WhiteLED = smd LED [color="White (4500K)" package="0603 [SMD]"]
  BlueLED = smd LED [color="Blue (525nm)" package="0805 [SMD]"]
  BlueLEDRes = Resistor [tolerance=±5% resistance=681 package=THT]
  WhiteLEDRes = Resistor [tolerance=±5% resistance=681 package=THT]
  GreenLED = smd LED [color="Green (565nm)" package="0805 [SMD]"]
  RedLED = smd LED [color="Red (635nm)" package="0805 [SMD]"]
  GreenLEDRes = Resistor [tolerance=±5% resistance=681 package=THT]
  RedLEDRes = Resistor [tolerance=±5% resistance=681 package=THT]
  Attacker = WeMos D1 Mini
  Requester = WeMos D1 Mini
  ML = WeMos D1 Mini
  Victim = WeMos D1 Mini
  UpButton = Momentary Switch [package=ksa_sealed_tac_switch]
  DownButton = Momentary Switch [package=ksa_sealed_tac_switch]
  AttackerButton = Momentary Switch [package=ksa_sealed_tac_switch]
  AttckerButtonRes = Resistor [tolerance=±5% resistance=10k package=THT]
  UpButtonREs = Resistor [tolerance=±5% resistance=10k package=THT]
  DownButtonRes = Resistor [tolerance=±5% resistance=10k package=THT]

nets:
  N1: VictimOLED.SDA, Victim.D1
  N2: VictimOLED.SCK, Victim.D2
  3.3V: VictimOLED.VDD, AttackerOLED.VDD, RequesterOLED.VDD, Attacker.3V3, Requester.3V3, ML.3V3, Victim.3V3, AttckerButtonRes.Pin_1, UpButtonREs.Pin_0, DownButtonRes.Pin_0
  GND: VictimOLED.GND, AttackerOLED.GND, RequesterOLED.GND, WhiteLED.cathode, BlueLED.cathode, GreenLED.cathode, RedLED.cathode, Attacker.G, Requester.G, ML.G, Victim.G, UpButton.3, DownButton.3, AttackerButton.3
  N3: AttackerOLED.SDA, Attacker.D1
  N4: AttackerOLED.SCK, Attacker.D2
  N5: RequesterOLED.SDA, Requester.D1
  N6: RequesterOLED.SCK, Requester.D2
  N7: WhiteLED.anode, WhiteLEDRes.Pin_0, WhiteLEDRes.Pin_1, Victim.D0
  N8: BlueLED.anode, BlueLEDRes.Pin_1
  N9: BlueLEDRes.Pin_0, ML.D6
  N10: GreenLED.anode, GreenLEDRes.Pin_1
  N11: RedLED.anode, RedLEDRes.Pin_1
  N12: GreenLEDRes.Pin_0, ML.D5
  N13: RedLEDRes.Pin_0, ML.D0
  N14: Attacker.D5, AttackerButton.2
  N15: Requester.D0, UpButton.2
  N16: Requester.D5, DownButton.2
  N17: ML.RX, Victim.TX
  N18: ML.TX, Victim.RX
  N19: UpButton.1, UpButtonREs.Pin_1
  N20: DownButton.1, DownButtonRes.Pin_1
  N21: AttackerButton.1, AttckerButtonRes.Pin_0
